# Fritzing sketch receiver (saved by Fritzing 0.9.3b)
circuit board: 7cm x 3cm

parts:
  GY-NEO6MV2 = SUP500F [package=sup500f]
  Nano_Receiver = Arduino Nano (Rev3.0) (ICSP)
  NRF24 = NRF24L01+ Breakout Board
  3V_Source = Battery
  PPM_Connector = Dagu DGServo 9g header connector (female) [package=THT]
  3V_Source1 = Battery
  J3 = female pin header, 2 pins [form="♀ (female)"]
  PPM_Connector1 = Dagu DGServo 9g header connector (female) [package=THT]
  PPM_Connector2 = Dagu DGServo 9g header connector (female) [package=THT]
  PPM_Connector3 = Dagu DGServo 9g header connector (female) [package=THT]
  PPM_Connector4 = Dagu DGServo 9g header connector (female) [package=THT]
  J4 = female alternating pin header, 1 pin [form="♀ (female)"]
  J5 = female alternating pin header, 1 pin [form="♀ (female)"]
  J8 = female alternating pin header, 1 pin [form="♀ (female)"]
  J9 = female alternating pin header, 1 pin [form="♀ (female)"]
  J13 = female pin header, 13 pins [form="♀ (female)"]
  3V_Source2 = Battery
  3V_Source3 = Battery  # not connected
  3V_Source4 = Battery
  J14 = female alternating pin header, 1 pin [form="♀ (female)"]
  J15 = female alternating pin header, 1 pin [form="♀ (female)"]
  J16 = female alternating pin header, 1 pin [form="♀ (female)"]
  J17 = female alternating pin header, 1 pin [form="♀ (female)"]
  J18 = female alternating pin header, 1 pin [form="♀ (female)"]

nets (from the pcb view):
  N1: GY-NEO6MV2.RX-I, J5.pin1
  N2: GY-NEO6MV2.TX-O, Nano_Receiver.D4
  GND: GY-NEO6MV2.GND, Nano_Receiver.GND, PPM_Connector.gnd, 3V_Source1.-, J3.pin1, PPM_Connector1.gnd, PPM_Connector2.gnd, PPM_Connector3.gnd, PPM_Connector4.gnd, J13.pin13, 3V_Source4.-, J15.pin1
  VCC: GY-NEO6MV2.VCC, Nano_Receiver.VIN, 3V_Source1.+, 3V_Source4.+
  N3: Nano_Receiver.D2, PPM_Connector.pulse
  N4: Nano_Receiver.D3, J4.pin1
  N5: Nano_Receiver.D5, PPM_Connector1.pulse
  N6: Nano_Receiver.D6, PPM_Connector2.pulse
  N7: Nano_Receiver.D7, PPM_Connector3.pulse
  N8: Nano_Receiver.D8, PPM_Connector4.pulse
  N9: Nano_Receiver.D9, NRF24.CE
  N10: Nano_Receiver.D10, NRF24.CS
  N11: Nano_Receiver.D11/MOSI, NRF24.MOSI
  N12: Nano_Receiver.D12/MISO, NRF24.MISO
  N13: Nano_Receiver.RESET, J13.pin12
  N14: Nano_Receiver.5V, J13.pin11
  N15: Nano_Receiver.A7, J13.pin10
  N16: Nano_Receiver.A6, J13.pin9
  N17: Nano_Receiver.A5, J13.pin8
  N18: Nano_Receiver.A4, J13.pin7
  N19: Nano_Receiver.A3, J13.pin6
  N20: Nano_Receiver.A2, J13.pin5
  N21: Nano_Receiver.A1, J13.pin4
  N22: Nano_Receiver.A0, J13.pin3, J14.pin1, J18.pin1
  N23: Nano_Receiver.AREF, J13.pin2
  N24: Nano_Receiver.3V3, J13.pin1
  N25: Nano_Receiver.D13/SCK, NRF24.SCK, J8.pin1, J9.pin1
  N26: NRF24.GND, 3V_Source.-, 3V_Source2.-
  N27: NRF24.VCC, 3V_Source.+, 3V_Source2.+
  N28: J16.pin1, J17.pin1

notes:
  cmb87
  gps
  nrf
  3V  5V
  +
  -
