# Fritzing sketch generic_nrf24 (saved by Fritzing 0.9.3b)
circuit board: 7cm x 3cm

parts:
  Part2 = NRF24L01+ Breakout Board
  10uF = Capacitor Polarized [package=cpol-radial-10uf-25v]
  J1 = female pin header, 2 pins [form="♀ (female)"]
  Part3 = Arduino Nano (Rev3.0)
  J3 = female pin header, 1 pin [form="♀ (female)"]
  J4 = female pin header, 1 pin [form="♀ (female)"]
  J5 = female pin header, 1 pin [form="♀ (female)"]
  J6 = female pin header, 1 pin [form="♀ (female)"]
  J7 = female pin header, 1 pin [form="♀ (female)"]
  J8 = female pin header, 1 pin [form="♀ (female)"]
  J9 = female pin header, 1 pin [form="♀ (female)"]
  J10 = female pin header, 1 pin [form="♀ (female)"]
  J11 = female pin header, 1 pin [form="♀ (female)"]
  J12 = female pin header, 1 pin [form="♀ (female)"]
  J13 = female pin header, 6 pins [form="♀ (female)"]
  2_2 = Resistor [tolerance=±5% resistance=2.2k package=THT]
  4_7 = Resistor [tolerance=±5% resistance=4.7k package=THT]
  J14 = female pin header, 4 pins [form="♀ (female)"]
  J15 = female pin header, 1 pin [form="♀ (female)"]
  J16 = female pin header, 1 pin [form="♀ (female)"]
  J17 = female pin header, 1 pin [form="♀ (female)"]
  J18 = female pin header, 1 pin [form="♀ (female)"]
  J19 = female pin header, 1 pin [form="♀ (female)"]
  J21 = female pin header, 5 pins [form="♀ (female)"]
  J20 = female pin header, 5 pins [form="♀ (female)"]
  J22 = female pin header, 1 pin [form="♀ (female)"]
  J23 = female pin header, 1 pin [form="♀ (female)"]
  J24 = female pin header, 11 pins [form="♀ (female)"]

nets:
  GND: Part2.GND, 10uF.-, J1.pin1, Part3.GND, J11.pin1, J12.pin1, J13.pin3, J14.pin2, J21.pin1, J21.pin2, J21.pin3, J21.pin4, J21.pin5, J22.pin1, J23.pin1
  VCC: Part2.VCC, 10uF.+, J1.pin2, Part3.VIN
  N1: Part2.CE, Part3.D10, J9.pin1, J10.pin1
  N2: Part2.CS, Part3.D9, J5.pin1, J6.pin1
  N3: Part2.SCK, Part3.D13/SCK, J7.pin1, J8.pin1
  N4: Part2.MOSI, Part3.D11/MOSI, J3.pin1, J4.pin1
  N5: Part2.MISO, Part3.D12/MISO
  N6: Part3.D2, 2_2.Pin_0
  N7: Part3.D3, J13.pin4, J14.pin3, J17.pin1, J18.pin1
  N8: Part3.D4, J20.pin5
  N9: Part3.D5, J20.pin4
  N10: Part3.D6, J20.pin3
  N11: Part3.D7, J20.pin2
  N12: Part3.D8, J20.pin1
  N13: Part3.5V, J24.pin11
  N14: Part3.A7, J24.pin10
  N15: Part3.A6, J24.pin9
  N16: Part3.A5, J24.pin8
  N17: Part3.A4, J24.pin7
  N18: Part3.A3, J24.pin6
  N19: Part3.A2, J24.pin5
  N20: Part3.A1, J24.pin4
  N21: Part3.A0, J24.pin3
  N22: Part3.AREF, J24.pin2
  N23: Part3.3V3, J24.pin1
  N24: J13.pin2, J14.pin1, J15.pin1, J16.pin1
  N25: J13.pin5, 2_2.Pin_1, 4_7.Pin_0, J14.pin4
  N26: 4_7.Pin_1, J19.pin1

notes:
  nrf24
  hc05
  +
  -
  2
  4
  10uF
  nano
  cmb87

// code stored in the sketch: generic_nrf.ino
/*
Arduino Wireless Network - Multiple NRF24L01 Tutorial
== Example 01 - Servo Control / Node 00 - Potentiometer ==
by Dejan, www.HowToMechatronics.com
Libraries:
nRF24/RF24, https://github.com/nRF24/RF24
nRF24/RF24Network, https://github.com/nRF24/RF24Network
*/
#include <RF24.h>
#include <RF24Network.h>
#include <SPI.h>
RF24 radio(10, 9); // nRF24L01 (CE,CSN)
RF24Network network(radio); // Include the radio in the network
const uint16_t this_node = 00; // Address of this node in Octal format ( 04,031, etc)
const uint16_t node01 = 01; 
void setup() {
SPI.begin();
radio.begin();
network.begin(90, this_node); //(channel, node address)
}
void loop() {
network.update();
unsigned long potValue = analogRead(A0); // Read the potentiometer value
unsigned long angleValue = map(potValue, 0, 1023, 0, 180); // Convert the value to 0-180
RF24NetworkHeader header(node01); // (Address where the data is going)
bool ok = network.write(header, &angleValue, sizeof(angleValue)); // Send the data
}
